# Fritzing sketch Project6 Fritzing (saved by Fritzing 0.9.0b)
breadboards: 1

parts:
  Part1 = Arduino Uno (Rev3)
  LED1 = smd LED [color="Red (633nm)" package="0805 [SMD]"]
  R3 = Resistor [tolerance=±5% resistance=10k package=THT]
  LED2 = smd LED [color="Yellow (585nm)" package="0603 [SMD]"]
  LED3 = smd LED [color="Green (555nm)" package="0603 [SMD]"]
  R4 = Resistor [tolerance=±5% resistance=220 package="1206 [SMD]"]
  R5 = Resistor [tolerance=±5% resistance=220 package="1206 [SMD]"]
  R6 = Resistor [tolerance=±5% resistance=220 package="1206 [SMD]"]
  R7 = Photocell (LDR) [package=THT]

nets:
  N1: Part1.A0, R3.Pin_0, R7.pin_1
  N2: Part1.D11_PWM/MOSI, LED1.anode
  N3: Part1.D12/MISO, LED2.anode
  N4: Part1.D13/SCK, LED3.anode
  N5: Part1.GND, R3.Pin_1, R4.Pin_1, R5.Pin_1, R6.Pin_1
  N6: Part1.5V, R7.pin_0
  N7: LED1.cathode, R6.Pin_0
  N8: LED2.cathode, R5.Pin_0
  N9: LED3.cathode, R4.Pin_0
